# Fritzing sketch load_cell (saved by Fritzing 0.8.5b)
breadboards: 2

parts:
  Part1 = Arduino Nano (Rev3.0)  # not connected
  U1 = POT [package=pot_mammoth]  # not connected
  R1 = Resistor [tolerance=±5% resistance=220 package=THT]
  IC1 = DIP - 16 pins [chip_label=INA125D package="DIP (Dual Inline) [THT]"]

nets:
  N1: R1.Pin_0, IC1.RG#8
  N2: R1.Pin_1, IC1.RG#7
  N3: IC1.V+, IC1.SLEEP
  N4: IC1.V-, IC1.IAREF
  N5: IC1.VREF_OUT, IC1.VREF5
  N6: IC1.VG, IC1.Sense

notes:
  VIN-
  VIN+
  A0 Arduino
  5V
  0V

custom parts:
  DIP - 16 pins: A DIP stand-in part for whatever IC you want. With 16 pins on a 300mil dual inline package (DIP) footprint.
